// Digital circuit top.dig as structural Verilog
module top (
  input  [3:0] A,
  input  [3:0] B,
  input  [3:0] operador,
  input  [3:0] clk,
  output [7:0] segmentos,
  output [1:0] comunes
);

  wire u_divFreq_v_nclk;
  wire [3:0] multiplexer_1_out, u_binTobcd_d, u_binTobcd_u;
  wire [5:0] u_sum_res_v_s;

  sum_res_v u_sum_res_v (
    .A(A[0]), .B(B[0]), .op(operador[0]), .S(u_sum_res_v_s[0]), .Cout(u_sum_res_v_s[4]), .sig(segmentos[7]));
  binTobcd #(.applicationType("IVERILOG"), .Code_File("/home/luisvaca/Documentos/MATE/bcdbinariodec/binTobcd.v")) u_binTobcd (
    .bin(u_sum_res_v_s), .U(u_binTobcd_u), .D(u_binTobcd_d[1:0]));
  divFreq_v u_divFreq_v (.CLK(clk[0]), .nCLK(u_divFreq_v_nclk));
  Multiplexer #(.Bits(4)) multiplexer_1 (
    .sel(u_divFreq_v_nclk), .in_0(u_binTobcd_u), .in_1(u_binTobcd_d), .out(multiplexer_1_out));
  bcdTo7seg_v u_bcdTo7seg_v (.BCD(multiplexer_1_out[0]), .seg7(segmentos[0]));
  Demultiplexer demultiplexer_1 (.sel(u_divFreq_v_nclk), .in(1'b1), .out_0(comunes[0]), .out_1(comunes[1]));
  // Pins of 1 and 4 bits meet at A
  // Pins of 1 and 4 bits meet at B
  // Pins of 1 and 4 bits meet at operador
  // Pins of 1 and 4 bits meet at clk
  // Pins of 2 and 4 bits meet at u_binTobcd_d
  // Pins of 1 and 4 bits meet at multiplexer_1_out
  // Pins of 1 and 4 bits meet at u_sum_res_v_s[3:0]
  // Pins of 5 and 6 bits meet at u_sum_res_v_s
  // Pins of 1 and 7 bits meet at segmentos[6:0]

  // Other names for the same wires on the sheet: signo = segmentos[7]
endmodule

/* Code of binTobcd:
module binTobcd(
	input wire [5:0] bin, //entrada binaria de 5 datos, con cout
	output [3:0] U, //salida unidades del binario
	output [1:0] D	//salida decenas maximo hasta 3 del binario
);
	
wire d0;
wire d1;
wire u0;
wire u1;
wire u2;
wire u3;
assign d0 = (A & C) | (A & B);
assign d1 = (~A & B & D) | (~A & B & C) | (A & ~B & ~C) | (B & C & D);
assign u3 = (~A & B & ~C & ~D) | (A & ~B & ~C & D) | (A & B & C & ~D);
assign u2 = (~A & ~B & C) | (~A & C & D) | (A & ~C & ~D) | (A & B & ~C);
assign u1 = (~A & ~B & D) | (~A & B & C & ~D) | (A & ~B & ~C & ~D) | (A & B & ~C & D) | (~B & C & D);
assign u0 = E;

assign [3:0]U = {u3,u2,u1,u0}; //asignacion de los arrays
assign [1:0]D = {d1,d0}; 

endmodule
*/
