// Digital circuit deviacionMotor.dig as structural Verilog
module deviacionMotor (
  input  [8:0] distancia,
  input  clk,
  input  activar,
  output m_izquierdo,
  output m_derecho
);

  wire comparator_1_eq, comparator_1_gt, d_ff_2_nq, or_1_out;
  wire [8:0] d_ff_1_q;

  D_FF #(.Bits(9)) d_ff_1 (.D(distancia), .C(clk), .Q(d_ff_1_q));  // open: nQ
  D_FF d_ff_2 (.D(d_ff_2_nq), .C(~activar), .Q(m_derecho), .nQ(d_ff_2_nq));
  Comparator #(.Bits(9)) comparator_1 (.a(d_ff_1_q), .b(9'hf), .gt(comparator_1_gt), .eq(comparator_1_eq));  // open: lt
  or or_1 (or_1_out, comparator_1_gt, comparator_1_eq);
  and and_1 (m_izquierdo, m_derecho, or_1_out);
endmodule
