// Digital circuit seguidoresDeLinea.dig as structural Verilog
module seguidoresDeLinea (
  input  [8:0] distancia,
  input  clk,
  input  activar,
  input  respSeguidorLinea1,
  input  respSeguidorLinea2,
  output m_izquierdo,
  output m_derecho
);

  wire comparator_1_eq, comparator_1_gt, or_1_out;
  wire [8:0] d_ff_1_q;

  D_FF #(.Bits(9)) d_ff_1 (.D(distancia), .C(clk), .Q(d_ff_1_q));  // open: nQ
  Comparator #(.Bits(9)) comparator_1 (.a(d_ff_1_q), .b(9'hf), .gt(comparator_1_gt), .eq(comparator_1_eq));  // open: lt
  or or_1 (or_1_out, comparator_1_gt, comparator_1_eq);
  and and_1 (m_derecho, activar, respSeguidorLinea2);
  and and_2 (m_izquierdo, respSeguidorLinea1, activar, or_1_out);
endmodule
